# Fritzing sketch soundspeed (saved by Fritzing 0.9.3b)
breadboards: 1

parts:
  Part1 = Arduino Uno (Rev3)
  U1 = TMP36 [package=to-92]
  hc-sr1 = hc-sr04

nets:
  N1: Part1.A0, U1.VOUT
  N2: Part1.D9_PWM, hc-sr1.Echo
  N3: Part1.D10_PWM/SS, hc-sr1.Trig
  VCC: Part1.5V, U1.VCC, hc-sr1.VCC
  GND: Part1.GND, U1.GND, hc-sr1.GND

// code stored in the sketch: soundspeed.ino
#include <Ultrasonic.h>



// defines pins numbers
  const int trigPin = 9;
  const int echoPin = 10;
  int sensorPin = 0;
  
// defines variables
 // float duration, s;
  

  void setup() {
    pinMode(trigPin, OUTPUT); // Sets the trigPin as an Output
    pinMode(echoPin, INPUT); // Sets the echoPin as an Input
    Serial.begin(9600); // Starts the serial communication
  }

  void loop() {
    float ultraSread = 0;
    float tempread = 0;

    for (int i =0; i<100; i++) {
      // Clears the trigPin
      digitalWrite(trigPin, LOW);
      delayMicroseconds(2);
      // Sets the trigPin on HIGH state for 10 micro seconds
      digitalWrite(trigPin, HIGH);
      delayMicroseconds(10);
      digitalWrite(trigPin, LOW);

      // Reads the echoPin, returns the sound wave travel time in microseconds
      ultraSread += pulseIn(echoPin, HIGH);
      tempread += analogRead(sensorPin);
    }
    float aveUS = ultraSread / 1000;
    float aveT = tempread / 100;
    
    
    
    // Returns the sound speed in m/s (0.19 is the sensor to internal box wall distance in m!!)
    float s = 2*0.19/(aveUS /1000000); // sound speed in m/s


    // getting the voltage reading from the temperature sensor 
    // int reading = analogRead(sensorPin);  
 
    // converting that reading to voltage, for 3.3v arduino use 3.3
    float voltage = aveT * 5./ 1023;
    //   voltage /= 1024.0; 

    float temperatureC = (voltage - 0.5) * 100 ;  //converting from 10 mv per degree wit 500 mV offset
                                                  //to degrees ((voltage - 500mV) times 100)

    
    Serial.print(temperatureC); 
    Serial.print(" ");
    Serial.println(s);
    delay(1000);
  }
